# Fritzing sketch project-15 (saved by Fritzing 0.9.4)
breadboards: 1

parts:
  Q1 = Basic FET P-Channel [package="TO220 [THT]"]
  U1 = Optocoupler [package=THT]
  Part1 = Arduino Uno (Rev3)
  BAT1 = BC9VPC [package=bc9vpc]
  C1 = Capacitor Polarized [package=cpol-radial-10uf-25v]
  M1 = DC Motor
  R1 = Resistor [tolerance=±5% resistance=220 package=THT]
  R2 = Resistor [tolerance=±5% resistance=1M package=THT]
  D1 = Schottky Diode [part_number=1N5817 package="300 mil [THT]"]

nets:
  N1: Q1.gate, U1.Pin_4, R2.Pin_0
  N2: Q1.drain, M1.pin_1, D1.anode
  N3: Q1.source, BAT1.V-, C1.-, R2.Pin_1
  N4: U1.Pin_1, R1.Pin_0
  N5: U1.Pin_2, Part1.GND
  N6: U1.Pin_5, BAT1.V+, C1.+, M1.pin_2, D1.cathode
  N7: Part1.D2, R1.Pin_1
